# Fritzing sketch watch_rev_3.0 (saved by Fritzing 0.9.0b)
circuit board: 3.2cm x 3.2cm
breadboards: 1

parts:
  VCC1 = Battery
  Q1 = MOSFET-PCHANNEL [package=sot23-3]
  I1 = 10uf inductor CBC3225T100MR [package=1210]
  D1 = DIODE-SCHOTTKY [package=sma-diode]
  R1 = Resistor [tolerance=±20% resistance=10k package="0603 [SMD]"]
  R2 = Resistor [tolerance=±20% resistance=47 package="0603 [SMD]"]
  LED1 = LEDs [package=led-0603]
  R3 = Resistor [tolerance=±5% resistance=100k package="0603 [SMD]"]
  U1 = MCP73831 [package=sot23-5]
  C2 = Capacitor [part_number=4.7uf package=0402-cap]
  C3 = Capacitor [part_number=0.1uf package=0402-cap]
  U3 = USB_AB [package=usb-ab-micro-smd]
  RFduino1 = RFduino SMT
  ZIF2 = Omron connector v2 [package=1x10-2mm-smd]
  U10 = MAX1722 [package=sot23-5]
  C4 = Capacitor [part_number=10uf package=0603-cap]
  C6 = Capacitor [part_number=100nf package=0402-cap]
  C8 = Capacitor [part_number=4.7uf package=0402-cap]
  C5 = Capacitor [part_number=10uf package=0402-cap]
  R5 = Resistor [package="0402 [SMD]"]
  C7 = Capacitor [part_number=0.22uf package=0402-cap]
  U9 = PCF8575C [package=so-24dw]
  U11 = LSM9DS0TR [package=QFN-24]
  U6 = DS3231 [package=so08]
  R4 = Resistor [package="0402 [SMD]"]

nets:
  GND: VCC1.-, R1.Pin_1, R3.Pin_1, U1.VSS, C2.2, C3.2, U3.GND, RFduino1.gnd, ZIF2.VSS_(GND), ZIF2.VSSA, U10.GND, C4.2, C6.2, C8.2, C5.2, U9.A1, U9.A2, U9.GND, U9.A0, U11.GND, U6.GND
  N1: VCC1.+, Q1.D, U1.VBAT, C2.1
  N2: Q1.G, D1.A, R3.Pin_0
  N3: Q1.S, I1.1, D1.C, U10.BATT
  N4: I1.2, U10.LX
  N5: R1.Pin_0, U1.PROG
  N6: R2.Pin_0, U1.VIN, U3.VBUS
  N7: R2.Pin_1, LED1.A
  N8: LED1.C, U1.STAT
  VDD: C3.1, RFduino1.vin, ZIF2.DISP, ZIF2.VDDA, ZIF2.VDD, ZIF2.EXTMODE, U10.OUT, C4.1, C6.1, C5.1, R5.Pin_1, U9.VCC, U11.Vdd, U11.Vdd_IO, U11.CS_G, U11.CS_XM, U6.Vcc, U6.VBAT, R4.Pin_1
  N9: U3.D+, RFduino1.gpio0, U9.INT
  N10: U3.D-, RFduino1.reset
  N11: U3.USBID, RFduino1.gpio1
  N12: RFduino1.gpio2, R5.Pin_0, U9.SCL, U11.SCL, U6.SCL
  N13: RFduino1.gpio3, U9.SDA, U11.SDA, U6.SDA, R4.Pin_0
  N14: RFduino1.gpio4, ZIF2.SCS
  N15: RFduino1.gpio5, ZIF2.SI
  N16: RFduino1.gpio6, ZIF2.SCLK
  N17: C8.1, U11.C1_XM
  N18: C7.1, U11.SETC_XM
  N19: C7.2, U11.SETP_XM
  N20: U9.PO0, U11.INT2_XM
  N21: U9.PO1, U11.INT1_XM
  N22: U9.PO2, U11.INT_G

custom parts:
  10uf inductor CBC3225T100MR: Fixed Inductors INDCTR HI CUR WND 1210 10uH 20%
  RFduino SMT: RFduino SMT board
  Omron connector v2: made from the data sheet for an Omron 653-XF2M-1015-1A and Sharp memory displays; pin compatible with LS013B7DH03/LS013B4DN04
  PCF8575C: PCF8575C I/O Expander.
  LSM9DS0TR: LSM9DS0TR from stmicro
  DS3231: I2C real-time clock with internal oscilator and batter backup
